# Fritzing sketch Untitled Sketch (saved by Fritzing 1.0.4)

parts:
  A1 = Waveshare 2.9 e-Paper [package=THT]
  SG1 = Buzzer 12mm
  S1 = Switch
  U1 = Voltage Regulator - 5V [package="TO220 [THT]"]
  CPU1 = NodeMCU ESP32 S Dev Kit [package=THT]

nets:
  N1: A1.pin_1, CPU1.P4
  N2: A1.pin_2, CPU1.P16
  N3: A1.pin_3, CPU1.P17
  N4: A1.pin_4, CPU1.P5
  N5: A1.pin_5, CPU1.P18
  N6: A1.pin_6, CPU1.P23
  GND: A1.pin_7, SG1.2, U1.GND, CPU1.GND
  N7: A1.pin_8, U1.output_voltage, CPU1.3.3V
  N8: SG1.1, CPU1.P27
  N9: S1.leg1, U1.input_voltage

custom parts:
  Switch: A generic switch.
  Voltage Regulator - 5V: 5V DC Voltage Regulator
  NodeMCU ESP32 S Dev Kit: Beschreibung Der AZ-Delivery ESP32 NodeMCU verfügt über WiFi+Bluetooth-Konnektivität, onboard CH340 und Tasten, die über die Erweiterungsheader E/A-Pins des ESP 32-S-Moduls zugänglich sind. Bei neuen Versionen wird anstelle des CP2102 der UART-Wandler CH340 verwendet. Besonderheiten Geringe Abmessungen, wodurch es leicht in Projekte integrierbar ist. Die Entwicklung ist leicht dank Lua-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
